# Fritzing sketch Poele (saved by Fritzing 0.6.4b)
breadboards: 1

parts:
  J1 = male pin header, 6 pins [form="♂ (male)"]
  J4 = male pin header, 6 pins [form="♂ (male)"]
  J3 = male pin header, 6 pins [form="♂ (male)"]
  J7 = shrouded pin header, 10 pins [form="♂ (shrouded male)"]
  R1 = Resistor [tolerance=±5% resistance=22k package="0805 [SMD]"]
  D4 = Rectifier Diode [part_number=1N4148 package="0805 [SMD]"]
  D3 = Rectifier Diode [part_number=1N4148 package="0805 [SMD]"]
  J2 = male pin header, 6 pins [form="♂ (male)"]
  R3 = Resistor [tolerance=±5% resistance=22k package="0805 [SMD]"]
  J9 = male pin header, 2 pins [form="♂ (male)"]
  C3 = Ceramic Capacitor [capacitance=470nF package="0805 [SMD, multilayer]"]
  R4 = Resistor [tolerance=±5% resistance=22k package="0805 [SMD]"]
  C4 = Ceramic Capacitor [capacitance=470nF package="0805 [SMD, multilayer]"]
  J10 = male pin header, 2 pins [form="♂ (male)"]
  Q4 = Basic FET N-Channel [part_number=BSS123 package=SMD_SOT-23]
  Q1 = Basic FET N-Channel [part_number=BSS123 package=SMD_SOT-23]
  Q3 = Basic FET N-Channel [part_number=BSS123 package=SMD_SOT-23]
  Q5 = Basic FET N-Channel [part_number=BSS123 package=SMD_SOT-23]
  Q2 = Basic FET N-Channel [part_number=BSS123 package=SMD_SOT-23]
  D1 = Rectifier Diode [part_number=1N4148 package="0805 [SMD]"]
  D6 = Rectifier Diode [part_number=1N4148 package="0805 [SMD]"]
  D7 = Rectifier Diode [part_number=1N4148 package="0805 [SMD]"]
  D2 = Rectifier Diode [part_number=1N4148 package="0805 [SMD]"]
  D5 = Rectifier Diode [part_number=1N4148 package="0805 [SMD]"]
  C1 = Tantalum Capacitor [capacitance=4.7µF package="B 3528 [SMD, tantalum]"]
  C5 = Tantalum Capacitor [capacitance=1µF package="A 3216 [SMD, tantalum]"]

nets:
  N1: J1.pin2, Q5.gate
  GND: J1.pin3, J4.pin3, J3.pin3, J7.pin1, J7.pin2, J7.pin3, J7.pin4, J7.pin5, J2.pin3, J9.pin1, C3.0, C4.0, J10.pin1, Q4.source, Q1.source, Q3.source, Q5.source, Q2.source, C1.-, C5.-
  3.3V: J1.pin4, R1.Pin_0, R3.Pin_0, R4.Pin_0, C1.+
  N2: J1.pin5, Q1.gate
  N3: J4.pin2, Q3.gate
  N4: J4.pin5, Q2.gate
  N5: J3.pin2, R3.Pin_1, J9.pin2, C3.1, D6.cathode
  N6: J3.pin5, R4.Pin_1, C4.1, J10.pin2, D7.cathode
  N7: J7.pin6, R1.Pin_1, D4.anode, D3.anode, J2.pin6, Q1.drain, D1.cathode, D1.anode, D6.anode, D7.anode, D2.anode, D5.anode, C5.+
  N8: J7.pin7, Q2.drain, D2.cathode
  N9: J7.pin8, D3.cathode, Q3.drain
  N10: J7.pin9, D4.cathode, Q4.drain
  N11: J7.pin10, Q5.drain, D5.cathode
  N12: J2.pin2, Q4.gate

notes:
  DoMini
  Jx
  1 : PWR (bat)
  2: DIO
  3: GND
  4: +3.3V
  5 : AIO
  6 : IRQ
  J1
  2 : DIO - Digital 4
  5 : AIO - Digital 14
  J2
  2 : DIO - Digital 5
  5 : AIO - Digital 15
  J3
  2 : DIO - Digital 6
  5 : AIO - Digital 16
  J4
  2 : DIO - Digital 7
  5 : AIO - Digital 17
  IRQ

custom parts:
  Rectifier Diode: A smd rectifier diode
  Basic FET N-Channel: A MOSFET N-Channel Transistor
